// Logisim project Full-adder_for_two_3-bit_values.circ as structural Verilog: 1 circuit, main circuit main
module main (
  input  First_value,
  input  second_bit,
  input  first_bit,
  input  Second_value,
  input  second_bit_2,
  input  first_bit_2
);

  wire and_1_out, and_2_out, and_3_out, and_4_out, and_5_out, or_1_out, or_2_out, xor_1_out, xor_2_out,
       xor_3_out, xor_4_out, xor_5_out;

  xor xor_1 (xor_1_out, first_bit, first_bit_2);
  xor xor_2 (xor_2_out, second_bit, second_bit_2);
  and and_1 (and_1_out, second_bit_2, second_bit);
  and and_2 (and_2_out, first_bit_2, first_bit);
  xor xor_3 (xor_3_out, xor_2_out, and_2_out);
  and and_3 (and_3_out, xor_2_out, and_2_out);
  xor xor_4 (xor_4_out, First_value, Second_value);
  and and_4 (and_4_out, First_value, Second_value);
  or or_1 (or_1_out, and_3_out, and_1_out);
  xor xor_5 (xor_5_out, xor_4_out, or_1_out);
  and and_5 (and_5_out, xor_4_out, or_1_out);
  or or_2 (or_2_out, and_5_out, and_4_out);
  // Probe on nothing
  // Probe on nothing
  // Probe on nothing
  // Probe on nothing

  // Notes on the sheet:
  //   third bit
  //   third bit
  //   Full-adder for two 3-bit values
  //   Titov
  //   Result
  //   forth bit
  //   third bit
  //   second bit
  //   first bit
endmodule
